// Logisim project Lab6.circ as structural Verilog: 1 circuit, main circuit main
module main (
  input  B3,
  input  A3,
  input  B2,
  input  A2,
  input  B1,
  input  A1,
  input  B0,
  input  A0,
  input  C0,
  output out_10,
  output out_11,
  output out_12,
  output out_13,
  output out_14,
  output out_15,
  output out_16,
  output out_17
);

  wire and_1_out, and_2_out, and_3_out, and_4_out, and_5_out, and_6_out, and_7_out, and_8_out, and_9_out,
       G0_out, G1_out, G2_out, G3_out, or_1_out, or_2_out, or_3_out, or_4_out, or_5_out, or_6_out, P0_out,
       P0C0_out, P1_out, P2_out, P3_out;

  xor P2 (P2_out, A2, B2);
  and G2 (G2_out, B2, A2);
  xor P1 (P1_out, B1, B1);
  and G1 (G1_out, B1, A1);
  xor P0 (P0_out, A0, B0);
  and G0 (G0_out, B0, A0);
  xor P3 (P3_out, A3, B3);
  and G3 (G3_out, B3, A3);
  and and_1 (and_1_out, C0, P0_out);
  and and_2 (and_2_out, C0, P0_out);
  and and_3 (and_3_out, C0, P0_out);
  or or_1 (or_1_out, G0_out, and_1_out);
  or or_2 (or_2_out, G0_out, and_3_out);
  or or_3 (or_3_out, G0_out, and_2_out);
  and P0C0 (P0C0_out, P0_out, C0);
  and and_4 (and_4_out, P1_out, or_1_out);
  and and_5 (and_5_out, P1_out, or_2_out);
  and and_6 (and_6_out, P1_out, or_3_out);
  xor S0 (out_17, P0_out, C0);
  or or_4 (or_4_out, G1_out, and_4_out);
  or or_5 (or_5_out, G1_out, and_5_out);
  or C2 (out_15, G1_out, and_6_out);
  or C1 (out_16, P0C0_out, G0_out);
  and and_7 (and_7_out, P2_out, or_4_out);
  and and_8 (and_8_out, P2_out, or_5_out);
  xor S1 (out_14, P1_out, out_16);
  or or_6 (or_6_out, G2_out, and_7_out);
  xor S2 (out_12, P2_out, out_15);
  or C3 (out_13, G2_out, and_8_out);
  and and_9 (and_9_out, P3_out, or_6_out);
  xor S3 (out_10, P3_out, out_13);
  or C4 (out_11, G3_out, and_9_out);
endmodule
