// Logisim project lab7.circ as structural Verilog: 1 circuit, main circuit main
module main (
  input  shiftleft,
  input  shiftright,
  input  I2,
  input  I1,
  input  I3,
  input  I4,
  input  in_7,
  input  in_8,
  output out_9,
  output out_10
);

  wire clock_1_out, d_ff_1_q, d_ff_2_q, d_ff_3_q, d_ff_4_q, multiplexer_1_out;

  Clock clock_1 (.out(clock_1_out));
  Multiplexer #(.select(2)) multiplexer_1 (
    .in0(d_ff_1_q), .in1(shiftright), .in2(d_ff_2_q), .in3(I4), .out(multiplexer_1_out), .sel({in_7, in_8}));
  D_Flip_Flop d_ff_1 (
    .D(multiplexer_1_out), .clk(clock_1_out), .Q(d_ff_1_q), .preset(out_9), .reset(out_10));  // open: Qn
  LED led_1 (.in(d_ff_1_q));
  Multiplexer #(.select(2)) multiplexer_2 (
    .in0(d_ff_2_q), .in1(d_ff_1_q), .in2(d_ff_3_q), .in3(I3), .out(out_9), .sel({in_7, in_8}));
  D_Flip_Flop d_ff_2 (.D(out_9), .clk(clock_1_out), .Q(d_ff_2_q), .reset(out_10));  // open: Qn, preset
  LED led_2 (.in(d_ff_2_q));
  D_Flip_Flop d_ff_3 (.D(out_9), .clk(clock_1_out), .Q(d_ff_3_q), .reset(out_10));  // open: Qn, preset
  Multiplexer #(.select(2)) multiplexer_3 (
    .in0(d_ff_3_q), .in1(d_ff_2_q), .in2(d_ff_4_q), .in3(I2), .out(out_9), .sel({in_7, in_8}));
  LED led_3 (.in(d_ff_3_q));
  D_Flip_Flop d_ff_4 (.D(out_9), .clk(clock_1_out), .Q(d_ff_4_q), .reset(out_10));  // open: Qn, preset
  Multiplexer #(.select(2)) multiplexer_4 (
    .in0(d_ff_4_q), .in1(d_ff_3_q), .in2(shiftleft), .in3(I1), .out(out_9), .sel({in_7, in_8}));
  LED led_4 (.in(d_ff_4_q));
endmodule
